// Logisim project 15.circ as structural Verilog: 1 circuit, main circuit main
module main (
  input  J,
  input  K,
  input  CLK,
  input  T,
  output Q,
  output Q_tilde,
  output Q_2,
  output Q_tilde_2,
  output Q_3,
  output Q_tilde_3
);

  wire clock_1_out, clock_2_out, clock_3_out;

  Clock clock_1 (.out(clock_1_out));
  Clock clock_2 (.out(clock_2_out));
  Clock clock_3 (.out(clock_3_out));
  J_K_Flip_Flop j_k_ff_1 (.J(J), .K(clock_3_out), .Q(Q), .Qn(Q_tilde));  // open: clk, preset, en, reset
  D_Flip_Flop d_ff_1 (.clk(CLK), .D(clock_1_out), .Q(Q_2), .Qn(Q_tilde_2));  // open: preset, en, reset
  T_Flip_Flop t_ff_1 (.clk(clock_2_out), .T(T), .Q(Q_3), .Qn(Q_tilde_3));  // open: preset, reset, en

  // Notes on the sheet:
  //   CLK
  //   D
  //   CLK
  //   JK Flip Flop
  //   D-Flip Flop
  //   T Flip Flop
endmodule
